// Logisim project MIPS - Single cycle.circ as structural Verilog: 7 circuits, main circuit main
module main (
);

  wire button_1_out, CLK;
  wire [2:0] funct;
  wire [7:3] Immediate;
  wire [15:0] PC;
  wire [15:8] Insrtuction;

  Clock clock_1 (.out(CLK));
  PC pc_1 (.Data__Instruction_Address(PC), .CLK(CLK), .Reset(button_1_out));  // open: Next_Address
  Button button_1 (.out(button_1_out));
  Instruction_Memory instruction_memory_1 (.Address(PC), .Data__Instruction({Insrtuction, Immediate, funct}));

  // Other names for the same wires on the sheet: Immediate[2:0] = funct; Insrtuction[7:0] = {Immediate, funct};
  //   Jump_Address[11:0] = {Insrtuction[11:8], Immediate, funct}; OP_CODE[3:0] = Insrtuction[15:12];
  //   Rd[1:0] = Immediate[7:6]; Rs[1:0] = Insrtuction[11:10]; Rt[1:0] = Insrtuction[9:8];
  //   tunnel[2:0] = Immediate[5:3]

  // Notes on the sheet:
  //   J-Type
  //   I-Type
endmodule

module Control_Unit (
  input  [3:0] OP_CODE,
  output Register_Destination,
  output ALU_Source,
  output Memory_To_Register,
  output Register_Write,
  output Memory_Read,
  output Memory_Write,
  output Branch_Equal,
  output Branch_Not_Equal,
  output Jump,
  output ALU_OP_1,
  output ALU_OP_0,
  output LUI,
  output ANDI
);

  wire addi_out, not_1_out, not_2_out, not_3_out, not_4_out, not_5_out, not_6_out, not_7_out, not_8_out,
       not_9_out, not_10_out, not_11_out, not_12_out, not_13_out, not_14_out, not_15_out, not_16_out,
       not_17_out, not_18_out, not_19_out, not_20_out, not_21_out, not_22_out, not_23_out, not_24_out,
       ori_out;

  not not_1 (not_1_out, OP_CODE[1]);
  not not_2 (not_2_out, OP_CODE[2]);
  not not_3 (not_3_out, OP_CODE[0]);
  not not_4 (not_4_out, OP_CODE[3]);
  and R_fomat (Register_Destination, not_4_out, not_2_out, not_1_out, not_3_out);
  not not_5 (not_5_out, OP_CODE[0]);
  not not_6 (not_6_out, OP_CODE[2]);
  not not_7 (not_7_out, OP_CODE[3]);
  and u_lui (LUI, not_7_out, not_6_out, OP_CODE[1], not_5_out);
  not not_8 (not_8_out, OP_CODE[3]);
  not not_9 (not_9_out, OP_CODE[3]);
  not not_10 (not_10_out, OP_CODE[2]);
  and ori (ori_out, not_8_out, not_10_out, OP_CODE[1], OP_CODE[0]);
  not not_11 (not_11_out, OP_CODE[0]);
  not not_12 (not_12_out, OP_CODE[3]);
  not not_13 (not_13_out, OP_CODE[1]);
  and addi (addi_out, not_9_out, OP_CODE[2], not_13_out, not_11_out);
  not not_14 (not_14_out, OP_CODE[1]);
  not not_15 (not_15_out, OP_CODE[3]);
  and lw (Memory_Read, not_15_out, OP_CODE[2], OP_CODE[1], not_17_out);
  and u_andi (ANDI, not_12_out, OP_CODE[2], not_14_out, OP_CODE[0]);
  not not_16 (not_16_out, OP_CODE[3]);
  not not_17 (not_17_out, OP_CODE[0]);
  and sw (Memory_Write, not_16_out, OP_CODE[2], OP_CODE[1], OP_CODE[0]);
  not not_18 (not_18_out, OP_CODE[0]);
  not not_19 (not_19_out, OP_CODE[2]);
  not not_20 (not_20_out, OP_CODE[1]);
  and u_jump (Jump, OP_CODE[3], not_19_out, not_20_out, not_18_out);
  not not_21 (not_21_out, OP_CODE[1]);
  not not_22 (not_22_out, OP_CODE[2]);
  and beq (Branch_Equal, OP_CODE[3], not_22_out, not_21_out, OP_CODE[0]);
  not not_23 (not_23_out, OP_CODE[0]);
  not not_24 (not_24_out, OP_CODE[2]);
  and bne (Branch_Not_Equal, OP_CODE[3], not_24_out, OP_CODE[1], not_23_out);
  or or_1 (ALU_Source, ori_out, addi_out, ANDI, Memory_Read, Memory_Write);
  or or_2 (Register_Write, Register_Destination, LUI, ori_out, addi_out, ANDI, Memory_Read);
  or or_3 (ALU_OP_1, Register_Destination, ori_out, ANDI);
  or or_4 (ALU_OP_0, Branch_Equal, ANDI, ori_out, Branch_Not_Equal);

  assign Memory_To_Register = Memory_Read;
endmodule

module Instruction_Memory (
  input  [15:0] Address,
  output [15:0] Data__Instruction
);

  ROM #(.addrWidth(16), .dataWidth(16)) rom_1 (.addr(Address), .data(Data__Instruction));  // open: sel

  // Notes on the sheet:
  //   Instruction Memory
endmodule

module PC (
  input  [15:0] Next_Address,
  input  CLK,
  input  Reset,
  output [15:0] Data__Instruction_Address
);

  Register #(.width(16)) PC (.D(Next_Address), .Q(Data__Instruction_Address), .clk(CLK), .clr(Reset));  // open: en
endmodule

module Register_File (
  input  [15:0] Write_Data,
  input  [1:0] Read_Register_1,
  input  [1:0] Write_Register,
  input  [1:0] Read_Register_2,
  input  Register_Write,
  input  CLK,
  output [15:0] Data_Register_1,
  output [15:0] Data_Register_2
);

  wire and_1_out, and_2_out, and_3_out, and_4_out, decoder_1_out0, decoder_1_out1, decoder_1_out2,
       decoder_1_out3;
  wire [15:0] register_1_q, register_2_q, register_3_q, register_4_q;

  Decoder #(.select(2), .enable("false")) decoder_1 (
    .out0(decoder_1_out0), .out1(decoder_1_out1), .out2(decoder_1_out2), .out3(decoder_1_out3),
    .sel(Write_Register));
  and and_1 (and_1_out, decoder_1_out0, Register_Write);
  and and_2 (and_2_out, decoder_1_out1, Register_Write);
  and and_3 (and_3_out, decoder_1_out2, Register_Write);
  and and_4 (and_4_out, decoder_1_out3, Register_Write);
  Register #(.width(16)) register_1 (.D(Write_Data), .en(and_1_out), .Q(register_1_q), .clk(CLK));  // open: clr
  Register #(.width(16)) register_2 (.D(Write_Data), .en(and_2_out), .Q(register_2_q), .clk(CLK));  // open: clr
  Register #(.width(16)) register_3 (.D(Write_Data), .en(and_3_out), .Q(register_3_q), .clk(CLK));  // open: clr
  Register #(.width(16)) register_4 (.D(Write_Data), .en(and_4_out), .Q(register_4_q), .clk(CLK));  // open: clr
  Multiplexer #(.select(2), .width(16)) multiplexer_1 (
    .in0(register_1_q), .in1(register_2_q), .in2(register_3_q), .in3(register_4_q), .out(Data_Register_1),
    .sel(Read_Register_1));  // open: en
  Multiplexer #(.select(2), .width(16)) multiplexer_2 (
    .in0(register_1_q), .in1(register_2_q), .in2(register_3_q), .in3(register_4_q), .out(Data_Register_2),
    .sel(Read_Register_2));  // open: en
endmodule

module ALU (
  input  [15:0] IN2,
  input  [15:0] IN1,
  input  [2:0] SWITCH,
  output [15:0] RESULT,
  output Zero
);

  wire comparator_1_lt, or_2_out;
  wire [15:0] adder_1_out, and_1_out, bit_extender_1_out, or_1_out, shifter_1_out, shifter_2_out,
       shifter_3_out, subtractor_1_out;

  assign or_1_out = IN1 | IN2;  // OR_Gate or_1, 16 bits wide
  assign and_1_out = IN1 & IN2;  // AND_Gate and_1, 16 bits wide
  Adder #(.width(16)) adder_1 (.a(IN1), .b(IN2), .out(adder_1_out));  // open: cin, cout
  Subtractor #(.width(16)) subtractor_1 (.a(IN1), .b(IN2), .out(subtractor_1_out));  // open: bin, bout
  Shifter #(.width(16)) shifter_1 (.in(IN1), .\dist (4'b0001), .out(shifter_1_out));
  Shifter #(.width(16), .shift("lr")) shifter_2 (.in(IN1), .\dist (4'b0001), .out(shifter_2_out));
  Shifter #(.width(16), .shift("ar")) shifter_3 (.in(IN1), .\dist (4'b0001), .out(shifter_3_out));
  Comparator #(.width(16)) comparator_1 (.a(IN1), .b(IN2), .lt(comparator_1_lt));  // open: gt, eq
  assign bit_extender_1_out = {{15{1'b0}}, comparator_1_lt};  // Bit_Extender bit_extender_1
  Multiplexer #(.select(3), .width(16)) multiplexer_1 (
    .in0(or_1_out), .in1(and_1_out), .in2(adder_1_out), .in3(subtractor_1_out), .in4(shifter_1_out),
    .in5(shifter_2_out), .in6(shifter_3_out), .in7(bit_extender_1_out), .out(RESULT), .sel(SWITCH));  // open: en
  or or_2 (or_2_out, RESULT[0], RESULT[1], RESULT[2], RESULT[3], RESULT[4], RESULT[5], RESULT[6], RESULT[7], RESULT[8], RESULT[9], RESULT[10], RESULT[11], RESULT[12], RESULT[13], RESULT[14], RESULT[15]);
  not not_1 (Zero, or_2_out);
endmodule

module ALU_Control (
  input  [2:0] FUNCT,
  input  [1:0] ALUop,
  input  ANDI,
  output [2:0] out_4
);

  wire [2:0] multiplexer_1_out;

  Multiplexer #(.width(3), .enable("false")) multiplexer_1 (
    .in0(3'b011), .in1(3'b101), .out(multiplexer_1_out), .sel(ANDI));
  Multiplexer #(.select(2), .width(3), .enable("false")) multiplexer_2 (
    .in0(3'b010), .in1(3'b011), .in2(FUNCT), .in3(multiplexer_1_out), .out(out_4), .sel(ALUop));
endmodule
